// Logisim project Desafio1_NAND_e_outros.circ as structural Verilog: 1 circuit, main circuit main
module main (
  input  in_1,
  input  in_2,
  input  B,
  input  Porta_NAND,
  input  B_2,
  output out_6
);

  wire not_1_out, not_2_out, not_3_out, not_4_out, or_1_out, or_2_out;

  not not_1 (not_1_out, in_1);
  not not_2 (not_2_out, in_2);
  not not_3 (not_3_out, Porta_NAND);
  not not_4 (not_4_out, B_2);
  or or_1 (or_1_out, not_2_out, B);
  or or_2 (or_2_out, not_3_out, not_4_out);
  and and_1 (out_6, or_1_out, not_1_out, or_2_out);
endmodule
