// Logisim project Desafio2_OR_e_GND.circ as structural Verilog: 1 circuit, main circuit main
module main (
  input  A,
  input  B,
  input  C,
  input  D,
  input  in_5,
  input  D_2,
  output out_7,
  output out_8
);

  wire and_1_out, and_2_out, nand_1_out, nand_2_out, nand_3_out, nand_4_out, nand_5_out, not_2_out,
       not_3_out, not_4_out, not_5_out, or_1_out, or_2_out;

  nand nand_1 (nand_1_out, A, A);
  nand nand_2 (nand_2_out, B, B);
  nand nand_3 (nand_3_out, C, C);
  nand nand_4 (nand_4_out, D, D);
  not not_1 (out_8, D_2);
  not not_2 (not_2_out, nand_1_out);
  not not_3 (not_3_out, nand_2_out);
  not not_4 (not_4_out, nand_3_out);
  not not_5 (not_5_out, nand_4_out);
  and and_1 (and_1_out, not_2_out, not_3_out, 1'b0);
  and and_2 (and_2_out, not_4_out, 1'b0);
  nand nand_5 (nand_5_out, not_5_out, not_5_out);
  or or_1 (or_1_out, and_1_out, and_2_out);
  or or_2 (or_2_out, and_1_out, or_1_out, and_2_out, nand_5_out, 1'b0);
  not not_6 (out_7, or_2_out);
  // also tied to GND on the sheet: in_5

  // Notes on the sheet:
  //   Se o cara entendeu, vai ver que só precisa mecher um botão
  //   Neste Desafio se introduz a porta NOR, o conceito de GND (estado zero Fixo) e a habilidade do cara perceber que na verdade este circuito todo é igual a:
  //   INTRODUZINDO A NOR
endmodule
