// Logisim project Fase1_and_three_inputs.circ as structural Verilog: 1 circuit, main circuit main
module main (
  input  in_1,
  input  in_2,
  input  in_3
);

  wire and_1_out, and_2_out;

  and and_1 (and_1_out, in_1, in_2);
  and and_2 (and_2_out, and_1_out, in_3);
  LED led_1 (.in(and_2_out));

  // Notes on the sheet:
  //   in_2: pull=up
endmodule
