// Logisim project Fase3_NAND.circ as structural Verilog: 1 circuit, main circuit main
module main (
  input  in_1,
  input  in_2,
  input  in_3,
  output out_4
);

  wire and_1_out, nand_1_out, nand_2_out, not_1_out, not_3_out;

  // AND_Gate and_1 has open pins: out=and_1_out
  not not_1 (not_1_out, in_3);
  // NOT_Gate not_2 has open pins: in=and_1_out, out=open
  nand nand_1 (nand_1_out, in_1, in_2);
  not not_3 (not_3_out, in_1);
  nand nand_2 (nand_2_out, not_3_out, not_1_out);
  // NAND_Gate nand_3 is placed but not wired
  and and_2 (out_4, nand_1_out, nand_2_out);

  // Notes on the sheet:
  //   ISSO
  //   Se o cara entendeu, vai ver que só precisa mecher um botão
  //   IGUAL A ISSO
endmodule
